// Logisim project RISCV32.circ as structural Verilog: 14 circuits, main circuit RISCV
module RISCV (
  input  in_1,
  input  in_2
);

  wire CL, comparator_black_box_1_p4, IsLoad, IsSLT, IsStore, IsWord, not_1_out, registerfile_1_p7, RegWE, TI;
  wire [1:0] multiplexer_2_out, OPt;
  wire [3:0] ALUOP, csdecoder_1_csout, CSWord, multiplexer_3_out;
  wire [4:0] IsLUI, reggen_1_rd, reggen_1_rs1, reggen_1_rs2, registerfile_1_p8;
  wire [19:0] multiplexer_2_out_2;
  wire [31:0] A, bit_extender_1_out, byteselector_1_dataout, byteshifter_1_dataout, immgen_1_outimm,
       multiplexer_1_out, pcadd_1_pc4, ram_1_data, register_1_q, registerfile_1_p1, risc_vprogramrom_1_p2;
  wire [31:5] registerfile_1_p8_2;
  wire [31:22] multiplexer_2_out_3;

  Clock clock_1 (.out(CL));
  Register #(.width(32)) register_1 (.D(pcadd_1_pc4), .clk(CL), .Q(register_1_q), .clr(in_2));  // open: en
  PCAdd pcadd_1 (.PC(register_1_q), .PC4(pcadd_1_pc4));
  // RISC_VProgramROM risc_vprogramrom_1: pin names not known; wires that end beside it: register_1_q, risc_vprogramrom_1_p2
  ReadAndWrite readandwrite_1 (
    .OP(risc_vprogramrom_1_p2), .OPType(OPt), .A(A), .IsLoad(IsLoad), .IsStore(IsStore), .RegWE(RegWE));
  LoadWord loadword_1 (.optype(OPt), .OP(risc_vprogramrom_1_p2), .CSWord(CSWord), .IsWord(IsWord));
  OPDecode opdecode_1 (.OP(risc_vprogramrom_1_p2), .OpType(OPt), .IsLUI(IsLUI), .TakeImm(TI));
  ALUOpGen aluopgen_1 (.OP(risc_vprogramrom_1_p2), .optype(OPt), .ALUOP(ALUOP), .IsSLT(IsSLT));
  RegGen reggen_1 (.Op(risc_vprogramrom_1_p2), .IsLUI(IsLUI), .Rd(reggen_1_rd), .Rs1(reggen_1_rs1), .Rs2(reggen_1_rs2));
  ImmGen immgen_1 (.Op(risc_vprogramrom_1_p2), .OutImm(immgen_1_outimm));
  // RegisterFile registerfile_1: pin names not known; wires that end beside it: registerfile_1_p1, CL, RegWE, reggen_1_rd, reggen_1_rs1, reggen_1_rs2, registerfile_1_p7, {registerfile_1_p8_2, registerfile_1_p8}
  Multiplexer #(.width(32)) multiplexer_1 (
    .in0({registerfile_1_p8_2, registerfile_1_p8}), .in1(immgen_1_outimm), .out(multiplexer_1_out), .sel(TI));
  // Comparator_Black_Box comparator_black_box_1: pin names not known; wires that end beside it: registerfile_1_p7, {registerfile_1_p8_2, registerfile_1_p8}, IsSLT, comparator_black_box_1_p4
  // ALU alu_1: pin names not known; wires that end beside it: registerfile_1_p7, multiplexer_1_out, ALUOP, registerfile_1_p8, A
  assign bit_extender_1_out = {{31{1'b0}}, comparator_black_box_1_p4};  // Bit_Extender bit_extender_1
  Multiplexer #(.width(32)) multiplexer_2 (
    .in0(A), .in1(bit_extender_1_out), .out({multiplexer_2_out_3, multiplexer_2_out_2, multiplexer_2_out}),
    .sel(IsSLT));
  CSDecoder csdecoder_1 (.CSIn(multiplexer_2_out), .CSOut(csdecoder_1_csout));
  ByteShifter byteshifter_1 (
    .DataIn({registerfile_1_p8_2, registerfile_1_p8}), .CSIn(multiplexer_2_out), .IsWord(IsWord),
    .DataOut(byteshifter_1_dataout));
  Multiplexer #(.width(4)) multiplexer_3 (.in0(csdecoder_1_csout), .in1(CSWord), .out(multiplexer_3_out), .sel(IsWord));
  RAM ram_1 (
    .addr(multiplexer_2_out_2[7:0]), .data(ram_1_data[7:0]), .sel(multiplexer_3_out[0]), .clk(CL),
    .ld(IsLoad), .clr(in_1));
  ByteSelector byteselector_1 (
    .DataIn(ram_1_data), .CSIn(multiplexer_2_out), .IsWord(IsWord), .DataOut(byteselector_1_dataout));
  Multiplexer #(.width(32)) multiplexer_4 (
    .in0(byteselector_1_dataout), .in1({multiplexer_2_out_3, multiplexer_2_out_2, multiplexer_2_out}),
    .out(registerfile_1_p1), .sel(not_1_out));
  not not_1 (not_1_out, IsLoad);
  // Pins of 8 and 20 bits meet at multiplexer_2_out_2
  // Pins of 8 and 32 bits meet at ram_1_data
  // Pins of 1 and 4 bits meet at multiplexer_3_out

  // Notes on the sheet:
  //   contents of risc_vprogramrom_1 (hex, n*v repeats v):
  //   ## cycles = 84   ## setting random start values for each register  # x1 = 361192250 lui x1, 88182
  //   addi x1, x1, -1222 # x2 = 148195846 lui x2, 36181 addi x2, x2, -1530 # x3 = -1738519596 lui x3,
  //   -424443 addi x3, x3, -1068 # x4 = -423595077 lui x4, -103417 addi x4, x4, 955 # x5 = 1054720235 lui
  //   x5, 257500 addi x5, x5, 235 # x6 = -1715185695 lui x6, -418747 addi x6, x6, 2017 # x7 = -204929724
  //   lui x7, -50032 addi x7, x7, 1348 # x8 = 1028152018 lui x8, 251014 addi x8, x8, -1326 # x9 =
  //   -1488891227 lui x9, -363499 addi x9, x9, 677 # x10 = -1727594106 lui x10, -421776 addi x10, x10, 390
  //   # x11 = 1354753952 lui x11, 330750 addi x11, x11, 1952 # x12 = 1971378999 lui x12, 481294 addi x12,
  //   x12, -1225 # x13 = 1814106855 lui x13, 442897 addi x13, x13, 743 # x14 = -1245828724 lui x14,
  //   -304157 addi x14, x14, -1652 # x15 = -1804510824 lui x15, -440554 addi x15, x15, -1640 # x16 = 1882
  //   addi x16, x16, 1882 # x17 = 630 addi x17, x17, 630 # x18 = 1850 addi x18, x18, 1850 # x19 = 1969
  //   addi x19, x19, 1969 # x20 = 844 addi x20, x20, 844 # x21 = 89 addi x21, x21, 89 # x22 = 717 addi
  //   x22, x22, 717 # x23 = 1500 addi x23, x23, 1500 # x24 = 522 addi x24, x24, 522 # x25 = 788 addi x25,
  //   x25, 788 # x26 = 5 addi x26, x26, 5 # x27 = 1967 addi x27, x27, 1967 # x28 = 684 addi x28, x28, 684
  //   # x29 = 1958 addi x29, x29, 1958 # x30 = 1596 addi x30, x30, 1596 # x31 = 1518 addi x31, x31, 1518
  //   ## testing sw and lw on randomly chosen registers  sw x5, 250(x16) lw x5, 250(x16) sw x7, 664(x28)
  //   lw x7, 664(x28) sw x8, 1247(x22) lw x8, 1247(x22) sw x4, 1651(x21) lw x4, 1651(x21) sw x11,
  //   1270(x29) lw x11, 1270(x29) sw x7, 1522(x16) lw x7, 1522(x16) sw x13, 1067(x22) lw x13, 1067(x22) sw
  //   x10, 960(x30) lw x10, 960(x30) sw x3, 1980(x23) lw x3, 1980(x23) sw x7, 854(x29) lw x7, 854(x29) sw
  //   x6, 134(x31) lw x6, 134(x31) sw x5, 431(x19) lw x5, 431(x19) sw x1, 1470(x18) lw x1, 1470(x18) sw
  //   x4, 422(x31) lw x4, 422(x31) sw x0, 12(x20) lw x0, 12(x20) sw x8, 287(x19) lw x8, 287(x19) sw x11,
  //   319(x26) lw x11, 319(x26) sw x9, 433(x27) lw x9, 433(x27) sw x5, 1337(x27) lw x5, 1337(x27) sw x1,
  //   1648(x25) lw x1, 1648(x25)
endmodule

module PCAdd (
  input  [31:0] PC,
  output [31:0] PC4
);

  // Incrementer #(.width(30)) incrementer_1: pin names not known; wires that end beside it: PC[31:2], PC4[31:2]

  assign PC4[1:0] = PC[1:0];

  // Notes on the sheet:
  //   Increments the counter by 4
endmodule

module OPDecode (
  input  [31:0] OP,
  output [1:0] OpType,
  output [4:0] IsLUI,
  output TakeImm
);

  wire and_1_out, and_2_out, not_1_out, not_2_out;

  not not_1 (not_1_out, OP[5]);
  not not_2 (not_2_out, OP[4]);
  and and_1 (and_1_out, OP[5], not_2_out);
  or or_1 (OpType[0], not_1_out, OP[2]);
  or or_2 (TakeImm, not_1_out, not_2_out, OP[2]);
  or or_3 (OpType[1], OP[2], and_1_out);
  and and_2 (and_2_out, OpType[0], OpType[1]);
  assign IsLUI = {{4{and_2_out}}, and_2_out};  // Bit_Extender bit_extender_1

  // Notes on the sheet:
  //   Corresponds to bits 5, 4, and 2
  //   Converts the instruction opcode into a two bit optype
endmodule

module ImmGen (
  input  [31:0] Op,
  output [31:0] OutImm
);

  wire [1:0] opdecode_1_optype;
  wire [31:0] bit_extender_1_out, bit_extender_2_out, bit_extender_3_out;

  assign bit_extender_1_out = {{20{Op[31]}}, Op[31:20]};  // Bit_Extender bit_extender_1
  assign bit_extender_2_out = {{20{Op[31]}}, {Op[31:25], Op[11:7]}};  // Bit_Extender bit_extender_2
  assign bit_extender_3_out = {{12{1'b0}}, Op[31:12]};  // Bit_Extender bit_extender_3
  Multiplexer #(.select(2), .width(32)) multiplexer_1 (
    .in0(bit_extender_1_out), .in1(bit_extender_1_out), .in2(bit_extender_2_out),
    .in3({bit_extender_3_out[19:0], bit_extender_3_out[31:20]}), .out(OutImm), .sel(opdecode_1_optype));
  OPDecode opdecode_1 (.OP(Op), .OpType(opdecode_1_optype));  // open: IsLUI, TakeImm

  // Notes on the sheet:
  //   Bits 7-31 of the instruction
  //   hold all potential imm bits
  //   Bits 0-6 hold the opcode;
  //   however, we only need 3 to decode
  //   I-type branch
  //   S-type branch
  //   U-type branch
  //   Branch 00 corresponds to R type
  //    (which doesn't use an imm), so the
  //   I-type imm is used as an arbitrary value
endmodule

module RegGen (
  input  [31:0] Op,
  input  [4:0] IsLUI,
  output [4:0] Rd,
  output [4:0] Rs1,
  output [4:0] Rs2
);

  wire [4:0] not_1_out;

  assign not_1_out = ~IsLUI;  // NOT_Gate not_1, 5 bits wide
  assign Rs1 = Op[19:15] & not_1_out;  // AND_Gate and_1, 5 bits wide
  assign Rs2 = Op[24:20] & not_1_out;  // AND_Gate and_2, 5 bits wide

  assign Rd = Op[11:7];

  // Notes on the sheet:
  //   Register Source 1 bits
  //   Register Destination bits
  //   Register Source 2 bits
endmodule

module SetLessThan (
  input  [31:0] A,
  input  [31:0] B
);

  // Comparator_Black_Box comparator_black_box_1: pin names not known; wires that end beside it: A, B
endmodule

module CalcMemAdd (
  input  [31:0] OP,
  output calcMemAddr
);

  wire and_1_out, and_2_out, not_1_out, not_2_out, not_3_out, not_4_out;
  wire [1:0] opdecode_1_optype;

  OPDecode opdecode_1 (.OP(OP), .OpType(opdecode_1_optype));  // open: IsLUI, TakeImm
  not not_1 (not_1_out, opdecode_1_optype[1]);
  not not_2 (not_2_out, opdecode_1_optype[0]);
  not not_3 (not_3_out, OP[14]);
  not not_4 (not_4_out, OP[12]);
  and and_1 (and_1_out, not_1_out, opdecode_1_optype[0], not_3_out, not_4_out);
  and and_2 (and_2_out, opdecode_1_optype[1], not_2_out, not_3_out, not_4_out);
  or or_1 (calcMemAddr, and_1_out, and_2_out);

  // Notes on the sheet:
  //   Bits 0 and 2 of Funct3
endmodule

module LoadWord (
  input  [1:0] optype,
  input  [31:0] OP,
  output [3:0] CSWord,
  output IsWord
);

  wire and_1_out, and_2_out;

  and and_1 (and_1_out, OP[13], optype[0]);
  and and_2 (and_2_out, OP[13], optype[1]);
  assign CSWord = {{3{IsWord}}, IsWord};  // Bit_Extender bit_extender_1
  or or_1 (IsWord, and_1_out, and_2_out);
endmodule

module CSDecoder (
  input  [1:0] CSIn,
  output [3:0] CSOut
);

  wire not_1_out, not_2_out;

  not not_1 (not_1_out, CSIn[1]);
  not not_2 (not_2_out, CSIn[0]);
  and and_1 (CSOut[3], CSIn[1], CSIn[0]);
  and and_2 (CSOut[2], CSIn[1], not_2_out);
  and and_3 (CSOut[1], not_1_out, CSIn[0]);
  and and_4 (CSOut[0], not_1_out, not_2_out);

  // Notes on the sheet:
  //   Produces a one-hot encoding
  //   representing the byte to store in
  //   (only applicable to load/store byte)
endmodule

module ReadAndWrite (
  input  [31:0] OP,
  input  [1:0] OPType,
  input  [31:0] A,
  output IsLoad,
  output IsStore,
  output RegWE
);

  wire and_1_out, and_2_out, and_5_out, and_6_out, nor_1_out, not_1_out, not_2_out, not_3_out, not_4_out,
       not_5_out, not_6_out, not_7_out, not_8_out, or_1_out;

  nor nor_1 (nor_1_out, A[31], A[30], A[29], A[28], A[27], A[26], A[25], A[24], A[23], A[22]);
  not not_1 (not_1_out, OP[14]);
  not not_2 (not_2_out, OP[12]);
  not not_3 (not_3_out, OPType[1]);
  not not_4 (not_4_out, OPType[0]);
  not not_5 (not_5_out, OP[4]);
  and and_1 (and_1_out, not_1_out, not_2_out, not_3_out, OPType[0], not_5_out);
  and and_2 (and_2_out, not_1_out, not_2_out, OPType[1], not_4_out, not_5_out);
  and and_3 (IsLoad, and_1_out, nor_1_out);
  and and_4 (IsStore, and_2_out, nor_1_out);
  not not_6 (not_6_out, nor_1_out);
  not not_7 (not_7_out, and_2_out);
  and and_5 (and_5_out, and_1_out, not_6_out);
  and and_6 (and_6_out, and_2_out, not_6_out);
  or or_1 (or_1_out, and_5_out, and_6_out);
  not not_8 (not_8_out, or_1_out);
  and and_7 (RegWE, not_7_out, not_8_out);
endmodule

module ALUOpGen (
  input  [31:0] OP,
  input  [1:0] optype,
  output [3:0] ALUOP,
  output IsSLT
);

  wire and_1_out, and_2_out, and_3_out, and_4_out, and_5_out, and_6_out, and_7_out, and_8_out, and_9_out,
       and_10_out, and_11_out, and_12_out, not_1_out, not_2_out, not_3_out, not_4_out, not_5_out, not_6_out;

  not not_1 (not_1_out, OP[14]);
  not not_2 (not_2_out, OP[13]);
  not not_3 (not_3_out, OP[12]);
  not not_4 (not_4_out, OP[30]);
  not not_5 (not_5_out, optype[1]);
  not not_6 (not_6_out, optype[0]);
  and and_1 (and_1_out, OP[14], not_3_out, not_4_out, not_5_out, not_6_out);
  and and_2 (and_2_out, OP[14], OP[13], not_4_out, not_5_out, not_6_out);
  and and_3 (and_3_out, OP[14], OP[13], OP[12], not_5_out, optype[0]);
  and and_4 (and_4_out, not_1_out, not_2_out, not_3_out, OP[30], not_5_out, not_6_out);
  and and_5 (and_5_out, OP[14], not_3_out, not_4_out, not_5_out, not_6_out);
  and and_6 (and_6_out, OP[14], not_2_out, OP[12], OP[30], not_5_out, not_6_out);
  and and_7 (and_7_out, OP[14], OP[13], not_4_out, not_5_out, not_6_out);
  and and_8 (and_8_out, OP[14], OP[13], OP[12], not_5_out, optype[0]);
  and and_9 (and_9_out, not_1_out, not_2_out, OP[12], not_4_out, not_5_out, not_6_out);
  and and_10 (and_10_out, OP[14], not_2_out, OP[12], OP[30], not_5_out, not_6_out);
  and and_11 (and_11_out, OP[14], OP[13], not_4_out, not_5_out, not_6_out);
  and and_12 (and_12_out, OP[14], OP[13], OP[12], not_5_out, optype[0]);
  and and_13 (IsSLT, not_1_out, OP[13], not_3_out, not_4_out, not_5_out, not_6_out);
  or or_1 (ALUOP[3], and_1_out, and_2_out, and_3_out);
  or or_2 (ALUOP[2], and_4_out, and_5_out, and_6_out, and_7_out, and_8_out);
  or or_3 (ALUOP[1], and_9_out, and_10_out, and_11_out, and_12_out);

  assign ALUOP[0] = OP[12];
endmodule

module LUI (
  input  [31:0] OP
);
endmodule

module ByteSelector (
  input  [31:0] DataIn,
  input  [1:0] CSIn,
  input  IsWord,
  output [31:0] DataOut
);

  wire [7:0] multiplexer_1_out;
  wire [31:0] bit_extender_1_out;

  Multiplexer #(.select(2), .width(8)) multiplexer_1 (
    .in0(DataIn[7:0]), .in1(DataIn[15:8]), .in2(DataIn[23:16]), .in3(DataIn[31:24]), .out(multiplexer_1_out),
    .sel(CSIn));
  assign bit_extender_1_out = {{24{multiplexer_1_out[7]}}, multiplexer_1_out};  // Bit_Extender bit_extender_1
  Multiplexer #(.width(32)) multiplexer_2 (.in0(bit_extender_1_out), .in1(DataIn), .out(DataOut), .sel(IsWord));
endmodule

module ByteShifter (
  input  [31:0] DataIn,
  input  [1:0] CSIn,
  input  IsWord,
  output [31:0] DataOut
);

  wire [31:0] bit_extender_1_out, multiplexer_1_out;

  assign bit_extender_1_out = {{24{1'b0}}, DataIn[7:0]};  // Bit_Extender bit_extender_1
  Multiplexer #(.select(2), .width(32)) multiplexer_1 (
    .in0(bit_extender_1_out),
    .in1({bit_extender_1_out[31:16], bit_extender_1_out[7:0], bit_extender_1_out[15:8]}),
    .in2({bit_extender_1_out[31:24], bit_extender_1_out[7:0], bit_extender_1_out[23:8]}),
    .in3({bit_extender_1_out[7:0], bit_extender_1_out[31:8]}), .out(multiplexer_1_out), .sel(CSIn));
  Multiplexer #(.width(32)) multiplexer_2 (.in0(multiplexer_1_out), .in1(DataIn), .out(DataOut), .sel(IsWord));
endmodule
